# Fritzing sketch BlinkStopLightW (saved by Fritzing 0.9.2b)
breadboards: 1

parts:
  R1 = Resistor [tolerance=±5% resistance=220 package=THT]
  LED1 = LED - 3mm [color="Green (555nm)" package="3 mm [THT]"]
  LED2 = LED - 3mm [color="Yellow (595nm)" package="3 mm [THT]"]
  LED3 = LED - 3mm [color="Red (633nm)" package="3 mm [THT]"]
  R2 = Resistor [tolerance=±5% resistance=220 package=THT]
  R3 = Resistor [tolerance=±5% resistance=220 package=THT]
  Part1 = Arduino Uno (Rev3)

nets:
  N1: R1.Pin_0, Part1.D13/SCK
  N2: R1.Pin_1, LED1.anode
  N3: LED1.cathode, LED2.cathode, LED3.cathode, Part1.GND
  N4: LED2.anode, R2.Pin_1
  N5: LED3.anode, R3.Pin_1
  N6: R2.Pin_0, Part1.D11_PWM/MOSI
  N7: R3.Pin_0, Part1.D9_PWM

notes:
  Blink Stoplight
  Mark Heckler
  mark.heckler@oracle.com
  @MkHeck
