# Fritzing sketch BlinkW (saved by Fritzing 0.9.2b)
breadboards: 1

parts:
  R1 = Resistor [tolerance=±5% resistance=220 package=THT]
  LED1 = LED - 3mm [color="Green (555nm)" package="3 mm [THT]"]
  Part1 = Arduino Uno (Rev3)

nets:
  N1: R1.Pin_0, Part1.D13/SCK
  N2: R1.Pin_1, LED1.anode
  N3: LED1.cathode, Part1.GND

notes:
  Blink
  Mark Heckler
  mark.heckler@oracle.com
  @MkHeck
