# Fritzing sketch HCSR04BasicTestW (saved by Fritzing 0.9.2b)
breadboards: 1

parts:
  Part2 = SRF05 Ultrasonic Rangefinder
  Part1 = Arduino Uno (Rev3)

nets:
  VCC: Part2.VCC, Part1.5V
  N1: Part2.Trig, Part1.D8
  N2: Part2.Echo, Part1.D10_PWM/SS
  GND: Part2.GND, Part1.GND

notes:
  HC-SR04 Basic Test
  Mark Heckler
  mark.heckler@oracle.com
  @MkHeck
  NOTE: Red wire is from 5v pin.
