# Fritzing sketch HCSR04ThreeLightsW (saved by Fritzing 0.9.2b)
breadboards: 1

parts:
  Part2 = SRF05 Ultrasonic Rangefinder
  R4 = Resistor [tolerance=±5% resistance=220 package=THT]
  R5 = Resistor [tolerance=±5% resistance=220 package=THT]
  R6 = Resistor [tolerance=±5% resistance=220 package=THT]
  LED4 = LED - 3mm [color="Red (633nm)" package="3 mm [THT]"]
  LED5 = LED - 3mm [color="Yellow (595nm)" package="3 mm [THT]"]
  LED6 = LED - 3mm [color="Green (555nm)" package="3 mm [THT]"]
  Part1 = Arduino Uno (Rev3)

nets:
  VCC: Part2.VCC, Part1.5V
  N1: Part2.Trig, Part1.D8
  N2: Part2.Echo, Part1.D10_PWM/SS
  GND: Part2.GND, LED4.cathode, LED5.cathode, LED6.cathode, Part1.GND
  N3: R4.Pin_1, LED4.anode
  N4: R5.Pin_1, LED5.anode
  N5: R6.Pin_1, LED6.anode

notes:
  HC-SR04 Three Lights
  Mark Heckler
  mark.heckler@oracle.com
  @MkHeck
  NOTE: Red VCC wire is from 5v pin.
