# Fritzing sketch PiBlink (saved by Fritzing 0.9.2b)
breadboards: 1

parts:
  Raspberry_Pi1 = Raspberry Pi B rev2
  LED2 = LED - 3mm [color="Green (555nm)" package="3 mm [THT]"]
  R1 = Resistor [tolerance=±5% resistance=220 package="0402 [SMD]"]

nets:
  N1: Raspberry_Pi1.GND, LED2.cathode
  N2: Raspberry_Pi1.GPIO_9, R1.Pin_0
  N3: LED2.anode, R1.Pin_1

notes:
  PiBlink
  Mark Heckler
  mark.heckler@oracle.com
  @MkHeck
