# Fritzing sketch PiHCSR04BasicTest (saved by Fritzing 0.9.2b)
breadboards: 1

parts:
  Raspberry_Pi1 = Raspberry Pi B rev2
  Part1 = SRF05 Ultrasonic Rangefinder

nets:
  N1: Raspberry_Pi1.GPIO_2, Part1.Trig
  GND: Raspberry_Pi1.GND, Part1.GND
  N2: Raspberry_Pi1.GPIO_8, Part1.Echo
  5V: Raspberry_Pi1.5V, Part1.VCC

notes:
  Pi HC-SR04 Basic Test
  Mark Heckler
  mark.heckler@oracle.com
  @MkHeck
  NOTE: Red VCC wire is from 5v pin.
