# Fritzing sketch PiHCSR04ThreeLights (saved by Fritzing 0.9.2b)
breadboards: 1

parts:
  Raspberry_Pi1 = Raspberry Pi B rev2
  LED2 = LED - 3mm [color="Green (555nm)" package="3 mm [THT]"]
  R1 = Resistor [tolerance=±5% resistance=220 package="0402 [SMD]"]
  LED3 = LED - 3mm [color="Yellow (595nm)" package="3 mm [THT]"]
  LED4 = LED - 3mm [color="Red (633nm)" package="3 mm [THT]"]
  R2 = Resistor [tolerance=±5% resistance=220 package="0402 [SMD]"]
  R3 = Resistor [tolerance=±5% resistance=220 package="0402 [SMD]"]
  Part1 = SRF05 Ultrasonic Rangefinder

nets:
  N1: Raspberry_Pi1.GPIO_2, Part1.Trig
  N2: Raspberry_Pi1.GPIO_3, R3.Pin_0
  GND: Raspberry_Pi1.GND, LED2.cathode, LED3.cathode, LED4.cathode, Part1.GND
  N3: Raspberry_Pi1.GPIO_9, R1.Pin_0
  N4: Raspberry_Pi1.GPIO_8, Part1.Echo
  N5: Raspberry_Pi1.GPIO_7, R2.Pin_0
  5V: Raspberry_Pi1.5V, Part1.VCC
  N6: LED2.anode, R1.Pin_1
  N7: LED3.anode, R2.Pin_1
  N8: LED4.anode, R3.Pin_1

notes:
  Pi HC-SR04 Three Lights
  Mark Heckler
  mark.heckler@oracle.com
  @MkHeck
  NOTE: Red VCC wire is from 5v pin.
